// Logisim project main.circ as structural Verilog: 10 circuits, main circuit main
module main (
  input  Reset
);

  wire beq, clock_1_out, decoder_1_out0, decoder_1_out1, disp, jump, lui, lw, or_1_out, or_2_out, ori, RType,
       sw;
  wire [2:0] rom_1_data;
  wire [3:0] display_controller_1_bottom0, display_controller_1_bottom1, display_controller_1_bottom2,
       display_controller_1_bottom3, display_controller_1_top0, display_controller_1_top1,
       display_controller_1_top2, display_controller_1_top3;
  wire [4:0] addr;
  wire [7:0] alu_1_output, beq_1_address, jump_1_addrout, LoadAddr, lui_1_rd, MEM, ori_1_rdoutput, PC, r0,
       r1, rdValue, regSaveValue, rxValue;

  or or_1 (or_1_out, jump, beq);
  instr_counter instr_counter_1 (.LoadAddress(or_1_out), .AddressIn(LoadAddr), .reset(Reset), .AddressOut(PC));
  RAM_module ram_module_1 (.DataIn(rdValue), .Address(addr[3:0]), .MemWrite(sw), .Reset(Reset), .DataOut(MEM));
  or or_2 (or_2_out, RType, ori, lui, lw);
  Decoder #(.disabled(0)) decoder_1 (.out0(decoder_1_out0), .out1(decoder_1_out1), .sel(addr[4]), .en(or_2_out));
  Decoder #(.select(3), .enable("false")) decoder_2 (
    .out0(RType), .out1(disp), .out2(lui), .out3(ori), .out4(lw), .out5(sw), .out6(jump), .out7(beq),
    .sel(rom_1_data));
  Register u_r0 (.D(regSaveValue), .en(decoder_1_out0), .Q(r0), .clk(clock_1_out), .clr(Reset));
  Clock clock_1 (.out(clock_1_out));
  assign LoadAddr = beq ? beq_1_address : 8'bz;  // Controlled_Buffer controlled_buffer_1
  beq beq_1 (.offset(addr), .PC(PC), .r1(r0), .r0(r0), .address(beq_1_address));
  assign LoadAddr = jump ? jump_1_addrout : 8'bz;  // Controlled_Buffer controlled_buffer_2
  jump jump_1 (.PC(PC), .address(addr), .addrOut(jump_1_addrout));
  Register u_r1 (.D(regSaveValue), .en(decoder_1_out1), .Q(r1), .clk(clock_1_out), .clr(Reset));
  ROM rom_1 (.addr(PC), .data({rom_1_data, addr}), .sel(1'b1));
  Multiplexer #(.width(8), .enable("false")) multiplexer_1 (.in0(r0), .in1(r1), .out(rdValue), .sel(addr[4]));
  assign regSaveValue = RType ? alu_1_output : 8'bz;  // Controlled_Buffer controlled_buffer_3
  ALU alu_1 (.rdInput(rdValue), .rxInput(rxValue), .func(addr[2:0]), .en(RType), .Output(alu_1_output));
  ori ori_1 (.Imm(addr[3:0]), .rdInput(rdValue), .rdOutput(ori_1_rdoutput));
  assign regSaveValue = ori ? ori_1_rdoutput : 8'bz;  // Controlled_Buffer controlled_buffer_4
  assign regSaveValue = lui ? lui_1_rd : 8'bz;  // Controlled_Buffer controlled_buffer_5
  lui lui_1 (.Imm(addr[3:0]), .rd(lui_1_rd));
  assign regSaveValue = lw ? MEM : 8'bz;  // Controlled_Buffer controlled_buffer_6
  Multiplexer #(.width(8), .enable("false")) multiplexer_2 (.in0(r0), .in1(r1), .out(rxValue), .sel(addr[3]));
  display_controller display_controller_1 (
    .Reset(Reset), .Disp(disp), .Value(rdValue[3:0]), .Digit(addr[1:0]), .Top0(display_controller_1_top0),
    .Bottom0(display_controller_1_bottom0), .Top1(display_controller_1_top1),
    .Bottom1(display_controller_1_bottom1), .Top2(display_controller_1_top2),
    .Bottom2(display_controller_1_bottom2), .Top3(display_controller_1_top3),
    .Bottom3(display_controller_1_bottom3));
  _7_Segment_Display u_7_segment_display_1 (
    .g(display_controller_1_top3[3]), .f(display_controller_1_top3[2]), .a(display_controller_1_top3[1]),
    .b(display_controller_1_top3[0]), .e(display_controller_1_bottom3[0]),
    .d(display_controller_1_bottom3[1]), .c(display_controller_1_bottom3[2]),
    .dp(display_controller_1_bottom3[3]));
  _7_Segment_Display u_7_segment_display_2 (
    .g(display_controller_1_top1[3]), .f(display_controller_1_top1[2]), .a(display_controller_1_top1[1]),
    .b(display_controller_1_top1[0]), .e(display_controller_1_bottom1[0]),
    .d(display_controller_1_bottom1[1]), .c(display_controller_1_bottom1[2]),
    .dp(display_controller_1_bottom1[3]));
  _7_Segment_Display u_7_segment_display_3 (
    .g(display_controller_1_top2[3]), .f(display_controller_1_top2[2]), .a(display_controller_1_top2[1]),
    .b(display_controller_1_top2[0]), .e(display_controller_1_bottom2[0]),
    .d(display_controller_1_bottom2[1]), .c(display_controller_1_bottom2[2]),
    .dp(display_controller_1_bottom2[3]));
  _7_Segment_Display u_7_segment_display_4 (
    .g(display_controller_1_top0[3]), .f(display_controller_1_top0[2]), .a(display_controller_1_top0[1]),
    .b(display_controller_1_top0[0]), .e(display_controller_1_bottom0[0]),
    .d(display_controller_1_bottom0[1]), .c(display_controller_1_bottom0[2]),
    .dp(display_controller_1_bottom0[3]));

  // Other names for the same wires on the sheet: imm[3:0] = addr[3:0]; offset[4:0] = addr; RFunc[2:0] = addr[2:0];
  //   rx = addr[3]; rd = addr[4]

  // Notes on the sheet:
  //   contents of rom_1 (hex, n*v repeats v):
  //   63 71 9 11 9
  //   Output Display
endmodule

// RAM
module RAM_module (
  input  [7:0] DataIn,
  input  [3:0] Address,
  input  Reset,
  input  MemWrite,
  output [7:0] DataOut
);

  wire clock_1_out, not_1_out;

  not not_1 (not_1_out, MemWrite);
  Clock clock_1 (.out(clock_1_out));
  assign DataOut = MemWrite ? DataIn : 8'bz;  // Controlled_Buffer controlled_buffer_1
  RAM #(.addrWidth(4)) ram_1 (
    .addr(Address), .data(DataOut), .sel(1'b1), .clk(clock_1_out), .ld(not_1_out), .clr(Reset));
endmodule

// IC
module instr_counter (
  input  LoadAddress,
  input  [7:0] AddressIn,
  input  reset,
  output [7:0] AddressOut
);

  wire clock_1_out, not_1_out;

  not not_1 (not_1_out, LoadAddress);
  Counter #(.ongoal("stay")) counter_1 (
    .load(LoadAddress), .D(AddressIn), .count(not_1_out), .Q(AddressOut), .clk(clock_1_out), .clr(reset));  // open: carry
  Clock clock_1 (.out(clock_1_out));
endmodule

module ALU (
  input  [7:0] rdInput,
  input  [7:0] rxInput,
  input  [2:0] func,
  input  en,
  output [7:0] Output
);

  wire [7:0] adder_1_out, and_1_out, negator_1_out, not_1_out, or_1_out, shifter_1_out, shifter_2_out,
       xor_1_out;

  assign or_1_out = rdInput | rxInput;  // OR_Gate or_1, 8 bits wide
  assign xor_1_out = rdInput ^ rxInput;  // XOR_Gate xor_1, 8 bits wide
  assign and_1_out = rdInput & rxInput;  // AND_Gate and_1, 8 bits wide
  Adder adder_1 (.a(rdInput), .b(rxInput), .out(adder_1_out), .cin(1'b0));  // open: cout
  Shifter #(.shift("lr")) shifter_1 (.in(rxInput), .\dist (3'b001), .out(shifter_1_out));
  Shifter #(.shift("ar")) shifter_2 (.in(rxInput), .\dist (3'b001), .out(shifter_2_out));
  assign not_1_out = ~rxInput;  // NOT_Gate not_1, 8 bits wide
  Negator negator_1 (.in(rxInput), .out(negator_1_out));
  Multiplexer #(.select(3), .width(8)) multiplexer_1 (
    .in0(or_1_out), .in1(xor_1_out), .in2(and_1_out), .in3(adder_1_out), .in4(shifter_1_out),
    .in5(shifter_2_out), .in6(not_1_out), .in7(negator_1_out), .out(Output), .sel(func), .en(en));
endmodule

// LUI
module lui (
  input  [3:0] Imm,
  output [7:0] rd
);


  assign rd = {Imm, 4'b0000};
endmodule

// ORI
module ori (
  input  [3:0] Imm,
  input  [7:0] rdInput,
  output [7:0] rdOutput
);

  assign rdOutput[3:0] = Imm | rdInput[3:0];  // OR_Gate or_1, 4 bits wide

  assign rdOutput[7:4] = rdInput[7:4];
endmodule

module beq (
  input  [7:0] r1,
  input  [7:0] r0,
  input  [4:0] offset,
  input  [7:0] PC,
  output [7:0] address
);

  wire [7:0] and_1_out;
  wire [7:7] comparator_1_eq;

  Comparator comparator_1 (.a(r0), .b(r1), .eq(comparator_1_eq[7]));  // open: gt, lt
  assign and_1_out = {3'b000, offset} & {8{comparator_1_eq[7]}};  // AND_Gate and_1, 8 bits wide
  Adder adder_1 (.a(and_1_out), .b(PC), .out(address), .cin(1'b1));  // open: cout
endmodule

// jmp
module jump (
  input  [7:0] PC,
  input  [4:0] address,
  output [7:0] addrOut
);


  assign addrOut = {PC[7:5], address};
endmodule

module display_controller (
  input  Reset,
  input  Disp,
  input  [3:0] Value,
  input  [1:0] Digit,
  output [3:0] Top0,
  output [3:0] Bottom0,
  output [3:0] Top1,
  output [3:0] Bottom1,
  output [3:0] Top2,
  output [3:0] Bottom2,
  output [3:0] Top3,
  output [3:0] Bottom3
);

  wire _0_out, _1_out, _2_out, _3_out, clock_1_out, clock_2_out, clock_3_out, clock_4_out, decoder_1_out0,
       decoder_1_out1, decoder_1_out2, decoder_1_out3;
  wire [3:0] register_1_q, register_2_q, register_3_q, register_4_q;

  Decoder #(.select(2), .enable("false")) decoder_1 (
    .out0(decoder_1_out0), .out1(decoder_1_out1), .out2(decoder_1_out2), .out3(decoder_1_out3), .sel(Digit));
  and _0 (_0_out, decoder_1_out0, Disp);
  and _1 (_1_out, decoder_1_out1, Disp);
  and _2 (_2_out, decoder_1_out2, Disp);
  and _3 (_3_out, decoder_1_out3, Disp);
  Register #(.width(4)) register_1 (.D(Value), .en(_0_out), .Q(register_1_q), .clk(clock_1_out), .clr(Reset));
  Clock clock_1 (.out(clock_1_out));
  Register #(.width(4)) register_2 (.D(Value), .en(_1_out), .Q(register_2_q), .clk(clock_2_out), .clr(Reset));
  Clock clock_2 (.out(clock_2_out));
  Register #(.width(4)) register_3 (.D(Value), .en(_2_out), .Q(register_3_q), .clk(clock_3_out), .clr(Reset));
  Clock clock_3 (.out(clock_3_out));
  Register #(.width(4)) register_4 (.D(Value), .en(_3_out), .Q(register_4_q), .clk(clock_4_out), .clr(Reset));
  Clock clock_4 (.out(clock_4_out));
  display_converter display_converter_1 (.Input(register_1_q), .Top(Top0), .Bottom(Bottom0));
  display_converter display_converter_2 (.Input(register_2_q), .Top(Top1), .Bottom(Bottom1));
  display_converter display_converter_3 (.Input(register_3_q), .Top(Top2), .Bottom(Bottom2));
  display_converter display_converter_4 (.Input(register_4_q), .Top(Top3), .Bottom(Bottom3));
endmodule

module display_converter (
  input  [3:0] Input,
  output [3:0] Top,
  output [3:0] Bottom
);

  Multiplexer #(.select(4), .width(8), .enable("false")) multiplexer_1 (
    .in0(8'h77), .in1(8'h41), .in2(8'h3b), .in3(8'h6b), .in4(8'h4d), .in5(8'h6e), .in6(8'h7e), .in7(8'h43),
    .in8(8'h7f), .in9(8'h6f), .in10(8'h5f), .in11(8'h7c), .in12(8'h36), .in13(8'h79), .in14(8'h3e),
    .in15(8'h1e), .out({Bottom, Top}), .sel(Input));

  // Notes on the sheet:
  //   0
  //   1
  //   2
  //   3
  //   4
  //   5
  //   6
  //   7
  //   8
  //   9
  //   a
  //   b
  //   c
  //   d
  //   e
  //   f
endmodule
